# Fritzing sketch T-Connector-Test (saved by Fritzing 0.9.10b)
circuit board: 8.46667cm x 5.64444cm

parts:
  TC-F-1 = T-Connector Female [package=THT]
  TC-M-1 = T-Connector Male [package=THT]

nets:
  GND: TC-F-1.GND, TC-M-1.GND
  VCC: TC-F-1.VCC, TC-M-1.VCC

custom parts:
  T-Connector Female: Red T - Female Connector for high current loads up to 60A.
  T-Connector Male: Red T - Male Connector for high current loads up to 60A.
